# Fritzing sketch External_Diagram (saved by Fritzing 0.9.3b)
breadboards: 1

parts:
  Part1 = Arduino Uno (Rev3)
  LCD1 = LCD screen
  R1 = TRIMPOT [package=trimpot-3mm]
  LED1 = LED - 5mm [color="Red (633nm)" package="5 mm [THT]"]
  LED2 = LED - 5mm [color="Red (633nm)" package="5 mm [THT]"]
  R2 = Resistor [tolerance=±5% resistance=220 package=THT]
  R3 = Resistor [tolerance=±5% resistance=220 package=THT]
  S1 = Pushbutton [package="[THT]"]
  R4 = Resistor [tolerance=±5% resistance=10k package=THT]
  Matrix_keypad1 = KEYPAD 4x4

nets:
  N1: Part1.A1, Matrix_keypad1.col1
  N2: Part1.A2, Matrix_keypad1.col2
  N3: Part1.A3, Matrix_keypad1.col3
  N4: Part1.A4/SDA, Matrix_keypad1.col4
  N5: Part1.A5/SCL, Matrix_keypad1.row1
  N6: Part1.D8, LCD1.E
  N7: Part1.D9_PWM, LCD1.DB4
  N8: Part1.D10_PWM/SS, LCD1.DB5
  N9: Part1.D11_PWM/MOSI, LCD1.DB6
  N10: Part1.D12/MISO, LCD1.DB7
  N11: Part1.D13/SCK, Matrix_keypad1.row2
  GND: Part1.GND, LCD1.VSS, LCD1.R/W, LCD1.LED-, R1.WIPER, R2.Pin_0, R3.Pin_0, R4.Pin_0
  N12: Part1.D2, S1.Pin_3, S1.Pin_4, R4.Pin_1
  N13: Part1.D3_PWM, Matrix_keypad1.row4
  N14: Part1.D4, LED2.anode
  N15: Part1.D5_PWM, LED1.anode
  N16: Part1.D6_PWM, Matrix_keypad1.row3
  N17: Part1.D7, LCD1.RS
  5V: Part1.5V, LCD1.VDD, LCD1.LED+, R1.CCW, S1.Pin_1, S1.Pin_2
  N18: LCD1.V0, R1.CW
  N19: LED1.cathode, R2.Pin_1
  N20: LED2.cathode, R3.Pin_1

notes:
  to Internal Arduino Ground
  to Internal Arduino Serial Pins

custom parts:
  KEYPAD 4x4: Matrix keypad 16 buttons, 4 rows x 4 columns
